# Fritzing sketch Maznio-lights (saved by Fritzing 0.9.4)
breadboards: 1

parts:
  Part1 = Arduino Uno (Rev3)
  R1 = Photocell (LDR) [package=THT]
  R2 = Resistor [tolerance=±5% resistance=10k package=THT]
  R3 = Resistor [tolerance=±5% resistance=10k package=THT]
  R4 = Resistor [tolerance=±5% resistance=100k package=THT]
  S1 = Round Pushbutton
  S2 = Round Pushbutton
  U1 = RELAY-SOLIDSTATE [package=relay-s108t02]
  U2 = RELAY-SOLIDSTATE [package=relay-s108t02]
  U3 = RELAY-SOLIDSTATE [package=relay-s108t02]
  U4 = RELAY-SOLIDSTATE [package=relay-s108t02]

nets:
  N1: Part1.A0, R1.pin_1, R2.Pin_0
  N2: Part1.A1, R3.Pin_0, R4.Pin_1
  N3: Part1.D8, U2.+
  N4: Part1.D9_PWM, U1.+
  N5: Part1.D10_PWM/SS, S1.leg1
  N6: Part1.D2, S2.leg1
  N7: Part1.D5_PWM, U4.+
  N8: Part1.D6_PWM, U3.+
  N9: Part1.5V, R1.pin_0
  N10: Part1.GND, R2.Pin_1, S1.leg0, S2.leg0

notes:
  BREAK
  start/stop
  Car input, 12+ Volts
